// Digital circuit 3 bit Register Set.dig as structural Verilog
module _3_bit_Register_Set (
  input  [1:0] WR_1_0,
  input  [2:0] WRD_2_0,
  input  CLK,
  input  [1:0] RA_1_0,
  input  [1:0] RB_1_0,
  input  WE,
  output [2:0] A_2_0,
  output [2:0] B_2_0
);

  wire A0, A1, A2, A3, D0, D1, D2, D3;
  wire [2:0] R0, R1, R2, R3;

  and and_1 (D3, A3, WE);
  and and_2 (D2, A2, WE);
  Decoder #(.Selector_Bits(2)) decoder_1 (.sel(WR_1_0), .out_0(A0), .out_1(A1), .out_2(A2), .out_3(A3));
  and and_3 (D1, A1, WE);
  and and_4 (D0, A0, WE);
  _3_bit_Register _3_bit_register_1 (.Din_2_0(WRD_2_0), .Sel(D3), .CLK(CLK), .Dout_3_0(R3));
  _3_bit_Register _3_bit_register_2 (.Din_2_0(WRD_2_0), .Sel(D2), .CLK(CLK), .Dout_3_0(R2));
  _3_bit_Register _3_bit_register_3 (.Din_2_0(WRD_2_0), .Sel(D1), .CLK(CLK), .Dout_3_0(R1));
  _3_bit_Register _3_bit_register_4 (.Din_2_0(WRD_2_0), .Sel(D0), .CLK(CLK), .Dout_3_0(R0));
  Multiplexer #(.Selector_Bits(2), .Bits(3)) multiplexer_1 (
    .sel(RA_1_0), .in_0(R0), .in_1(R1), .in_2(R2), .in_3(R3), .out(A_2_0));
  Multiplexer #(.Selector_Bits(2), .Bits(3)) multiplexer_2 (
    .sel(RB_1_0), .in_0(R0), .in_1(R1), .in_2(R2), .in_3(R3), .out(B_2_0));

  // Other names for the same wires on the sheet: WRD[2:0] = WRD_2_0
endmodule
