// Digital circuit 3 bit Register.dig as structural Verilog
module _3_bit_Register (
  input  [2:0] Din_2_0,
  input  Sel,
  input  CLK,
  output [2:0] Dout_3_0
);

  _1_bit_Register _1_bit_register_1 (.Din(Din_2_0[2]), .Sel(Sel), .CLK(CLK), .Dout(Dout_3_0[2]));
  _1_bit_Register _1_bit_register_2 (.Din(Din_2_0[1]), .Sel(Sel), .CLK(CLK), .Dout(Dout_3_0[1]));
  _1_bit_Register _1_bit_register_3 (.Din(Din_2_0[0]), .Sel(Sel), .CLK(CLK), .Dout(Dout_3_0[0]));

  // Other names for the same wires on the sheet: B0 = Dout_3_0[0]; B1 = Dout_3_0[1]; B2 = Dout_3_0[2];
  //   A0 = Din_2_0[0]; A1 = Din_2_0[1]; A2 = Din_2_0[2]
endmodule
