// Digital circuit 3bitALU.dig as structural Verilog
module _3bitALU (
  input  [1:0] OP_1_0,
  input  [2:0] A_2_0,
  input  [2:0] B_2_0,
  output [2:0] R_2_0
);

  wire [2:0] _3bitadder_1_r_2_0, _3bitor_1_r_2_0, _3bitshr_1_r_2_0;

  _3bitOR _3bitor_1 (.A_2_0(A_2_0), .B_2_0(B_2_0), .R_2_0(_3bitor_1_r_2_0));
  _3bitAdder _3bitadder_1 (.A_2_0(A_2_0), .B_2_0(B_2_0), .R_2_0(_3bitadder_1_r_2_0));  // open: Cout
  _3bitSHR _3bitshr_1 (.A_2_0(A_2_0), .B_2_0(B_2_0), .R_2_0(_3bitshr_1_r_2_0));
  Multiplexer #(.Selector_Bits(2), .Bits(3)) multiplexer_1 (
    .sel(OP_1_0), .in_0(_3bitor_1_r_2_0), .in_1(_3bitadder_1_r_2_0), .in_2(_3bitshr_1_r_2_0), .in_3(3'b000),
    .out(R_2_0));

  // Other names for the same wires on the sheet: A[2:0] = A_2_0; B[2:0] = B_2_0
endmodule
