// Digital circuit 3bitOR.dig as structural Verilog
module _3bitOR (
  input  [2:0] A_2_0,
  input  [2:0] B_2_0,
  output [2:0] R_2_0
);

  or or_1 (R_2_0[0], A_2_0[0], B_2_0[0]);
  or or_2 (R_2_0[1], A_2_0[1], B_2_0[1]);
  or or_3 (R_2_0[2], A_2_0[2], B_2_0[2]);
endmodule
