// Digital circuit 4 bit Program Counter Register.dig as structural Verilog
module _4_bit_Program_Counter_Register (
  input  [3:0] I_3_0,
  input  CLK,
  output [3:0] O_3_0
);

  _1_bit_Register _1_bit_register_1 (.Din(I_3_0[0]), .Sel(1'b1), .CLK(CLK), .Dout(O_3_0[0]));
  _3_bit_Register _3_bit_register_1 (.Din_2_0(I_3_0[3:1]), .Sel(1'b1), .CLK(CLK), .Dout_3_0(O_3_0[3:1]));

  // Other names for the same wires on the sheet: B0 = O_3_0[0]; B1[2:0] = O_3_0[3:1]; A0 = I_3_0[0];
  //   A1[2:0] = I_3_0[3:1]
endmodule
