// Digital circuit CPU Architecture.dig as structural Verilog
module CPU_Architecture (
  input  [3:0] WR_3_0,
  input  [15:0] WRD_15_0,
  input  WE,
  input  CLK,
  input  PC_EN,
  input  [3:0] RA2_3_0,
  input  ZF,
  input  SF,
  output [15:0] RD2_15_0,
  output [1:0] WR_1_0,
  output [1:0] R1_1_0,
  output [1:0] R2_1_0,
  output [2:0] A_2_0,
  output [2:0] B_2_0,
  output [2:0] R_2_0,
  output [3:0] JMP_ADDR_3_0
);

  wire CPU_CLK, Imm_sel, JMP_SEL, REG_EN;
  wire [0:0] Imm_val;
  wire [1:0] Op;
  wire [2:0] _3_bit_register_set_1_b_2_0;
  wire [3:0] _4_bit_pc_adder_1_o_3_0, _4_bit_program_counter_register_1_o_3_0, multiplexer_1_out;
  wire [6:0] XX1;
  wire [15:12] _9x16_sram_1_rd1_15_0;

  Multiplexer #(.Bits(4)) multiplexer_1 (
    .sel(JMP_SEL), .in_0(_4_bit_pc_adder_1_o_3_0), .in_1(JMP_ADDR_3_0), .out(multiplexer_1_out));
  _4_bit_PC_Adder _4_bit_pc_adder_1 (.I_3_0(_4_bit_program_counter_register_1_o_3_0), .O_3_0(_4_bit_pc_adder_1_o_3_0));
  _4_bit_Program_Counter_Register _4_bit_program_counter_register_1 (
    .I_3_0(multiplexer_1_out), .CLK(CLK), .O_3_0(_4_bit_program_counter_register_1_o_3_0));
  and and_1 (CPU_CLK, PC_EN, CLK);
  _9x16_SRAM _9x16_sram_1 (
    .RA1_3_0(_4_bit_program_counter_register_1_o_3_0), .RA2_3_0(RA2_3_0), .WR_3_0(WR_3_0),
    .WRD_15_0(WRD_15_0), .WE(WE), .CLK(CLK),
    .RD1_15_0({_9x16_sram_1_rd1_15_0, JMP_ADDR_3_0, Imm_val[0], XX1}), .RD2_15_0(RD2_15_0));
  _3_bit_Register_Set _3_bit_register_set_1 (
    .WR_1_0(JMP_ADDR_3_0[3:2]), .CLK(CPU_CLK), .WE(REG_EN), .WRD_2_0(R_2_0), .RA_1_0(JMP_ADDR_3_0[3:2]),
    .RB_1_0(JMP_ADDR_3_0[1:0]), .A_2_0(A_2_0), .B_2_0(_3_bit_register_set_1_b_2_0));
  _3bitALU _3bitalu_1 (.R_2_0(R_2_0), .OP_1_0(Op), .A_2_0(A_2_0), .B_2_0(B_2_0));
  _3bit_Control_Unit _3bit_control_unit_1 (
    .Opcode_3_0(_9x16_sram_1_rd1_15_0), .ZF(ZF), .SF(SF), .Op_1_0(Op), .REG_EN(REG_EN), .Imm_Sel(Imm_sel),
    .JMP_Sel(JMP_SEL));
  Multiplexer #(.Bits(3)) multiplexer_2 (
    .sel(Imm_sel), .in_0(_3_bit_register_set_1_b_2_0), .in_1({JMP_ADDR_3_0[1:0], Imm_val[0]}), .out(B_2_0));

  assign R1_1_0 = JMP_ADDR_3_0[3:2];
  assign R2_1_0 = JMP_ADDR_3_0[1:0];
  assign WR_1_0 = JMP_ADDR_3_0[3:2];

  // Other names for the same wires on the sheet: XX2[6:0] = XX1; XX1[7] = Imm_val[0];
  //   Imm_val[2:1] = JMP_ADDR_3_0[1:0]; JMP_ADDR[3:0] = JMP_ADDR_3_0; R2[1:0] = JMP_ADDR_3_0[1:0];
  //   R1[1:0] = JMP_ADDR_3_0[3:2]; A[2:0] = A_2_0; B[2:0] = B_2_0; R[2:0] = R_2_0; RD2[15:0] = RD2_15_0;
  //   WR[3:0] = WR_3_0; WRD[15:0] = WRD_15_0

  // Notes on the sheet:
  //   Register Mode(Type of Op = 00) = 2bit(Type of op) + 2bit(Op) + 2bit(Reg 1) + 2bit(Reg 2) + 8bit(Don't Care)
  //   Immediate Mode(Type of Op = 01) = 2bit(Type of op) + 2bit(Op) + 2bit(Reg 1) + 3bit(Imm Value) + 7bit(Don't Care)
  //   Jump Mode(Type of Op = 10) = 2bit(Type of op) + 2bit(Op) + 4bit(Address) + 8bit(Don't Care)
  //   OR (Op = 00), Add (Op = 01), SHR (Op = 10)
  //   JMP (Op = 00), JL (Op = 01)
  //   	JL START 1001001000000000 ZF=0,SF=1
  //   	OR R1,5 0100011010000000
  //   START:	OR R1,3 0100010110000000
  //   JMP-TO: 	ADD R1,R1 0001010100000000
  //   	JMP JMP-TO 1000001100000000
endmodule
